// Logisim project ula.circ as structural Verilog: 3 circuits, main circuit Ula
module Ula (
  input  [7:0] D0,
  input  [7:0] D1,
  input  MovHeight,
  input  [2:0] UlaCtrl,
  output Zero,
  output [7:0] D
);

  wire or_2_out;
  wire [3:0] adder_2_out, multiplexer_1_out, multiplexer_2_out, multiplexer_3_out;
  wire [7:0] ANDL, Mov, NOTL, ORL, SL, Soma, SR, Sub;

  Adder adder_1 (.a(D0), .b(D1), .out(Soma));  // open: cin, cout
  Subtractor subtractor_1 (.a(D0), .b(D1), .out(Sub));  // open: bin, bout
  assign ANDL = D0 & D1;  // AND_Gate and_1, 8 bits wide
  assign ORL = D0 | D1;  // OR_Gate or_1, 8 bits wide
  assign NOTL = ~D1;  // NOT_Gate not_1, 8 bits wide
  Shifter shifter_1 (.in(D0), .\dist (D1[2:0]), .out(SL));
  Shifter #(.shift("lr")) shifter_2 (.in(D0), .\dist (D1[2:0]), .out(SR));
  Multiplexer #(.width(4)) multiplexer_1 (.in0(D0[3:0]), .in1(D0[7:4]), .out(multiplexer_1_out), .sel(MovHeight));
  Multiplexer #(.width(4)) multiplexer_2 (.in0(D0[7:4]), .in1(D0[3:0]), .out(multiplexer_2_out), .sel(MovHeight));
  Multiplexer #(.width(4)) multiplexer_3 (.in0(D1[7:4]), .in1(D1[3:0]), .out(multiplexer_3_out), .sel(MovHeight));
  Adder #(.width(4)) adder_2 (.a(multiplexer_2_out), .b(multiplexer_3_out), .out(adder_2_out));  // open: cin, cout
  or or_2 (or_2_out, Sub[0], Sub[1], Sub[2], Sub[3], Sub[4], Sub[5], Sub[6], Sub[7]);
  Multiplexer #(.select(3), .width(8)) multiplexer_4 (
    .in0(Soma), .in1(Sub), .in2(ANDL), .in3(ORL), .in4(NOTL), .in5(SL), .in6(SR), .in7(Mov), .out(D),
    .sel(UlaCtrl));
  not not_2 (Zero, or_2_out);
  Multiplexer #(.width(8)) multiplexer_5 (
    .in0({adder_2_out, multiplexer_1_out}), .in1({multiplexer_1_out, adder_2_out}), .out(Mov), .sel(MovHeight));

  // Other names for the same wires on the sheet: MH = MovHeight
endmodule

module Registers (
  input  [1:0] Ra,
  input  [1:0] Rb,
  input  RegWrite,
  input  [7:0] Data,
  output [7:0] D0,
  output [7:0] D1
);

  wire Clk, WE0, WE1, WE2, WE3;
  wire [7:0] D0_t, D1_t, D2, D3, R0, R1, R2, R3;

  Clock clock_1 (.out(Clk));
  Demultiplexer #(.select(2)) demultiplexer_1 (.out0(WE0), .out1(WE1), .out2(WE2), .out3(WE3), .in(RegWrite), .sel(Ra));
  Demultiplexer #(.select(2), .width(8)) demultiplexer_2 (
    .out0(D0_t), .out1(D1_t), .out2(D2), .out3(D3), .in(Data), .sel(Ra));
  Register #(.trigger("high")) register_1 (.D(D0_t), .en(WE0), .clk(Clk), .Q(R0));  // open: clr
  Register #(.trigger("high")) register_2 (.D(D1_t), .en(WE1), .clk(Clk), .Q(R1));  // open: clr
  Register #(.trigger("high")) register_3 (.D(D2), .en(WE2), .clk(Clk), .Q(R2));  // open: clr
  Register register_4 (.D(D3), .en(WE3), .clk(Clk), .Q(R3));  // open: clr
  Multiplexer #(.select(2), .width(8)) multiplexer_1 (.in0(R0), .in1(R1), .in2(R2), .in3(R3), .out(D0), .sel(Ra));
  Multiplexer #(.select(2), .width(8)) multiplexer_2 (.in0(R0), .in1(R1), .in2(R2), .in3(R3), .out(D1), .sel(Rb));
endmodule

module main (
);

  wire Clk, MemRead, MemToReg, MemWrite, PcScr, RegWrite, UlaSrc, Zero;
  wire [1:0] Ra, Rb;
  wire [2:0] UlaCtrl;
  wire [3:0] Imm4bits;
  wire [7:0] Data, Imm, JumpAddr, MemOut, NextAddr, PC, PC4, R0, R1, UlaIn, UlaOut;

  ROM rom_1 (.addr(PC));  // open: data
  Multiplexer #(.width(8)) multiplexer_1 (.in0(JumpAddr), .in1(PC4), .out(NextAddr), .sel(PcScr));
  Adder adder_1 (.a(PC), .b(8'h4), .out(PC4));  // open: cin, cout
  Adder adder_2 (.a(PC4), .b(Imm), .out(JumpAddr));  // open: cin, cout
  Register register_1 (.D(NextAddr), .en(1'b1), .clk(Clk), .Q(PC));  // open: clr
  Clock clock_1 (.out(Clk));
  RAM ram_1 (.addr(UlaOut), .we(MemRead), .oe(MemWrite), .clk(Clk), .din(R1), .dout(MemOut));
  Registers registers_1 (.Ra(Ra), .Rb(Rb), .RegWrite(RegWrite), .Data(Data), .D0(R0), .D1(R1));
  Multiplexer #(.width(8)) multiplexer_2 (.in0(R1), .in1(Imm), .out(UlaIn), .sel(UlaSrc));
  assign Imm = {{4{Imm4bits[3]}}, Imm4bits};  // Bit_Extender bit_extender_1
  Ula ula_1 (.D0(R0), .D1(UlaIn), .MovHeight(Zero), .UlaCtrl(UlaCtrl), .Zero(Zero), .D(UlaOut));
  Multiplexer #(.width(8)) multiplexer_3 (.in0(UlaOut), .in1(MemOut), .out(Data), .sel(MemToReg));

  // Notes on the sheet:
  //   Escolhe o endereço
  //   Calculo PC+4
  //   Calculo do Pulo
  //   PC
  //   Pick ULA Input
  //   Immediate Sign Extension
  //   Pick Data to Write Back
endmodule
